# Fritzing sketch ServerSketch (saved by Fritzing 0.9.3b)

parts:
  U1 = NodeMCU V1.0
  Часть1 = NRF24L01+ Breakout Board
  C1 = Electrolytic Capacitor [capacitance=100μF package="0807 [SMD, electrolytic]"]

nets:
  N1: U1.D1, Часть1.IRQ
  N2: U1.D2, Часть1.CE
  3V3: U1.3V3, Часть1.VCC, C1.+
  GND: U1.GND, Часть1.GND, C1.-
  N3: U1.D5, Часть1.SCK
  N4: U1.D6, Часть1.MISO
  N5: U1.D7, Часть1.MOSI
  N6: U1.D8, Часть1.CS

custom parts:
  NodeMCU V1.0: ESP8266 based NodeMCU
